// Logisim project MajorityVoteCounter.circ as structural Verilog: 2 circuits, main circuit main
module main (
  input  P,
  input  T,
  input  V,
  input  X,
  input  S,
  input  Y,
  output Tie
);

  wire and_1_out, and_2_out, not_1_out, or_1_out;
  wire [3:0] Count;

  not not_1 (not_1_out, Count[2]);
  and and_1 (and_1_out, Count[0], Count[1]);
  and and_2 (and_2_out, P, not_1_out);
  YesVotes yesvotes_1 (.P(P), .T(T), .V(V), .X(X), .S(S), .Y(Y), .Count(Count));
  and and_3 (Tie, and_1_out, and_2_out);
  Hex_Digit_Display #(.decimalPoint("false")) hex_digit_display_1 (.value(Count));
  or or_1 (or_1_out, Tie, Count[2]);
  LED led_1 (.in(or_1_out));
endmodule

module YesVotes (
  input  P,
  input  T,
  input  V,
  input  X,
  input  S,
  input  Y,
  output [3:0] Count
);

  wire [3:0] Px, S1, S2, S3, S4, Sx, Tx, Vx, Xx, Yx;

  assign Px = {{3{1'b0}}, P};  // Bit_Extender bit_extender_1
  assign Vx = {{3{1'b0}}, V};  // Bit_Extender bit_extender_2
  assign Sx = {{3{1'b0}}, S};  // Bit_Extender bit_extender_3
  Adder #(.width(4)) adder_1 (.a(Px), .b(Vx), .out(S1), .cin(1'b0));  // open: cout
  Adder #(.width(4)) adder_2 (.a(S1), .b(Sx), .out(S2), .cin(1'b0));  // open: cout
  Adder #(.width(4)) adder_3 (.a(S2), .b(Tx), .out(S3), .cin(1'b0));  // open: cout
  assign Tx = {{3{1'b0}}, T};  // Bit_Extender bit_extender_4
  assign Xx = {{3{1'b0}}, X};  // Bit_Extender bit_extender_5
  assign Yx = {{3{1'b0}}, Y};  // Bit_Extender bit_extender_6
  Adder #(.width(4)) adder_4 (.a(S3), .b(Xx), .out(S4), .cin(1'b0));  // open: cout
  Adder #(.width(4)) adder_5 (.a(S4), .b(Yx), .out(Count), .cin(1'b0));  // open: cout
endmodule
